// Logisim project ALU .circ as structural Verilog: 1 circuit, main circuit main
module main (
  input  [23:0] in_1,
  input  Enable,
  input  [23:0] in_3,
  input  [1:0] ALU_op,
  output [23:0] \output ,
  output Zero_flag
);

  wire nor_1_out, subtractor_1_bout;
  wire [23:0] adder_1_out, and_1_out, multiplexer_1_out, subtractor_1_out;

  assign and_1_out = in_1 & in_3;  // AND_Gate and_1, 24 bits wide
  Adder #(.width(24)) adder_1 (.a(in_1), .b(in_3), .out(adder_1_out));  // open: cin, cout
  Subtractor #(.width(24)) subtractor_1 (
    .a(in_1), .b(in_3), .out(subtractor_1_out), .bout(subtractor_1_bout));  // open: bin
  Multiplexer #(.width(24)) multiplexer_1 (
    .in0(in_1), .in1(in_3), .out(multiplexer_1_out), .sel(subtractor_1_bout));  // open: en
  Multiplexer #(.select(2), .width(24)) multiplexer_2 (
    .in0(and_1_out), .in1(adder_1_out), .in2(subtractor_1_out), .in3(multiplexer_1_out), .out(\output ),
    .sel(ALU_op), .en(Enable));
  nor nor_1 (nor_1_out, \output [0], \output [1], \output [2], \output [3], \output [4], \output [5], \output [6], \output [7], \output [8], \output [9], \output [10], \output [11], \output [12], \output [13], \output [14], \output [15], \output [16], \output [17], \output [18], \output [19], \output [20], \output [21], \output [22], \output [23]);
  or or_1 (Zero_flag, nor_1_out, subtractor_1_bout);

  // Notes on the sheet:
  //   Rs
  //   Rt
  //   AND
  //   ADD
  //   SUB
endmodule
