// Logisim project Cond_Control.circ as structural Verilog: 1 circuit, main circuit main
module main (
  input  [1:0] Cond_bits,
  input  ZeroFlag,
  output out_3
);

  wire and_1_out, and_2_out, not_1_out, not_2_out, not_3_out;

  not not_1 (not_1_out, Cond_bits[0]);
  not not_2 (not_2_out, ZeroFlag);
  not not_3 (not_3_out, Cond_bits[1]);
  and and_1 (and_1_out, not_1_out, not_2_out);
  and and_2 (and_2_out, not_3_out, ZeroFlag);
  or or_1 (out_3, and_1_out, and_2_out);
endmodule
