// Logisim project Decoding_stage.circ as structural Verilog: 1 circuit, main circuit main
module main (
  input  [23:0] Instruction,
  output [1:0] Alu_op,
  output j,
  output memRd,
  output [1:0] cond_bits,
  output jr,
  output memWr,
  output jal,
  output AluSrc,
  output BEQ,
  output SF_BIT,
  output regWr,
  output regdst,
  output extOp,
  output WB,
  output [2:0] Rs,
  output [2:0] Rd,
  output [2:0] Rt,
  output [23:0] Sign_extended_imm
);

  wire or_1_out;
  wire [1:0] and_1_out;
  wire [23:0] bit_extender_1_out, bit_extender_2_out, main_1_out_2;

  and and_1 (and_1_out[0], ~Instruction[17], Instruction[18], Instruction[19], ~Instruction[20], Instruction[21]);  // AND_Gate
  and and_2 (and_1_out[1], ~Instruction[17], Instruction[18], Instruction[19], Instruction[20], ~Instruction[21]);  // AND_Gate
  or or_1 (or_1_out, and_1_out[0], and_1_out[1]);
  assign bit_extender_1_out = {{14{1'b0}}, Instruction[9:0]};  // Bit_Extender bit_extender_1
  assign bit_extender_2_out = {{7{1'b0}}, Instruction[16:0]};  // Bit_Extender bit_extender_2
  shifterby4_main main_1 (.in_1(bit_extender_2_out), .out_2(main_1_out_2));
  mainControl_main main_2 (
    .opcode(Instruction[21:17]), .Alu_Op(Alu_op), .j(j), .memRd(memRd), .jr(jr), .memWr(memWr), .jal(jal),
    .AluSrc(AluSrc), .BEQ(BEQ), .SF_BIT(Instruction[16]), .regWr(regWr), .regDst(regdst), .EXTop(extOp),
    .wb(WB), .sf_flag(SF_BIT));
  Multiplexer #(.width(3)) multiplexer_1 (
    .in0(Instruction[15:13]), .in1(3'b000), .out(Rs), .sel(or_1_out));  // open: en
  Multiplexer #(.select(2), .width(3)) multiplexer_2 (
    .in0(Instruction[12:10]), .in1(3'b111), .in2(3'b001), .out(Rt), .sel(and_1_out));  // open: in3, en
  Multiplexer #(.select(2), .width(24)) multiplexer_3 (
    .in0(bit_extender_1_out), .in1(bit_extender_2_out), .in2(main_1_out_2), .out(Sign_extended_imm),
    .sel(and_1_out));  // open: in3, en

  assign cond_bits = Instruction[23:22];
  assign Rd = Instruction[9:7];
endmodule
