// Logisim project ID-IF_BUFFER.circ as structural Verilog: 1 circuit, main circuit main
module main (
  input  [23:0] PC_1,
  input  [23:0] Instruction,
  input  EN,
  input  CLK,
  input  CLR,
  output [23:0] PC_1_OUT,
  output [23:0] Instruction_out
);

  Register #(.width(24)) register_1 (.D(PC_1), .en(EN), .Q(PC_1_OUT), .clk(CLK), .clr(CLR));
  Register #(.width(24)) register_2 (.D(Instruction), .en(EN), .Q(Instruction_out), .clk(CLK), .clr(CLR));
endmodule
