// Logisim project Mem.circ as structural Verilog: 1 circuit, main circuit main
module main (
  input  [23:0] Address,
  input  [23:0] Data_IN,
  input  MemRead,
  input  MemWrite,
  input  CLK,
  input  in_6,
  output [23:0] Data_OUT
);

  wire not_1_out, not_2_out, or_1_out;
  wire [23:0] controlled_buffer_1_out, ram_1_data;

  or or_1 (or_1_out, MemRead, MemWrite);
  RAM #(.addrWidth(24), .dataWidth(24)) ram_1 (
    .addr(Address), .data(ram_1_data), .sel(or_1_out), .clk(CLK), .ld(not_1_out), .clr(in_6));
  not not_1 (not_1_out, MemWrite);
  assign controlled_buffer_1_out = not_2_out ? ram_1_data : 24'bz;  // Controlled_Buffer controlled_buffer_1
  assign ram_1_data = MemWrite ? Data_IN : 24'bz;  // Controlled_Buffer controlled_buffer_2
  not not_2 (not_2_out, MemWrite);
endmodule
