// Logisim project PC_Control.circ as structural Verilog: 1 circuit, main circuit main
module main (
  input  J,
  input  JAL,
  input  BEQ,
  input  ZeroFlag,
  input  JR,
  output [1:0] PcSrc
);

  wire and_1_out, and_2_out, or_1_out;

  and and_1 (and_1_out, ~or_1_out, ~and_2_out, ~JR);  // AND_Gate
  and and_2 (and_2_out, BEQ, ZeroFlag);
  or or_1 (or_1_out, J, JAL);
  Priority_Encoder #(.select(2)) priority_encoder_1 (
    .in0(and_1_out), .in1(or_1_out), .in2(and_2_out), .in3(JR), .out(PcSrc), .en_in(1'b1));  // open: gs, en_out
endmodule
