// Logisim project control(1).circ as structural Verilog: 1 circuit, main circuit Control Unit
module Control_Unit (
  input  [3:0] opcode,
  input  [2:0] func,
  output reg_WR,
  output mem_WR,
  output mem_RD,
  output [2:0] mux_in_sel,
  output [2:0] ALU_op,
  output ALU_src,
  output [1:0] PC_mux,
  output DST_sel,
  output Eq,
  output nEq
);

  wire and_1_out, and_2_out, and_3_out, and_4_out, and_5_out, and_6_out, and_7_out, and_8_out, and_9_out,
       and_12_out, and_13_out, and_14_out, and_15_out, and_17_out, and_18_out, and_19_out, and_20_out,
       and_21_out, and_22_out, and_23_out, and_24_out, and_25_out, and_26_out, and_27_out, nor_1_out,
       not_1_out, or_1_out;

  and and_1 (and_1_out, func[0], func[1]);
  and and_2 (and_2_out, ~func[0], func[2]);  // AND_Gate
  or or_1 (or_1_out, and_1_out, and_2_out);
  and and_3 (and_3_out, opcode[0], ~opcode[1], opcode[2]);  // AND_Gate
  and and_4 (and_4_out, opcode[0], opcode[1], ~opcode[2], ~opcode[3]);  // AND_Gate
  or or_2 (DST_sel, opcode[0], opcode[1], opcode[2], opcode[3]);
  and and_5 (and_5_out, opcode[0], ~opcode[1], opcode[2]);  // AND_Gate
  not not_1 (not_1_out, opcode[3]);
  nor nor_1 (nor_1_out, func[0], func[1], func[2], ~opcode[0], ~opcode[1], ~opcode[2], ~opcode[3]);  // NOR_Gate
  and and_6 (and_6_out, ~opcode[0], opcode[1], ~opcode[3]);  // AND_Gate
  and and_7 (and_7_out, opcode[1], ~opcode[2], opcode[3]);  // AND_Gate
  and and_8 (and_8_out, opcode[0], ~opcode[1], ~opcode[2]);  // AND_Gate
  and and_9 (and_9_out, opcode[0], opcode[1], opcode[3]);
  and and_10 (mem_WR, ~opcode[0], opcode[1], opcode[2], opcode[3]);  // AND_Gate
  and and_11 (mem_RD, opcode[0], ~opcode[1], ~opcode[2], opcode[3]);  // AND_Gate
  and and_12 (and_12_out, func[0], func[1], ~opcode[0], ~opcode[1], ~opcode[2], ~opcode[3]);  // AND_Gate
  or or_3 (mux_in_sel[2], and_12_out, opcode[3], and_13_out);
  and and_13 (and_13_out, opcode[0], opcode[1]);
  and and_14 (and_14_out, ~opcode[0], opcode[1], opcode[2], ~opcode[3]);  // AND_Gate
  or or_4 (mux_in_sel[1], and_14_out, and_15_out);
  and and_15 (and_15_out, opcode[0], opcode[2], opcode[3]);
  and and_16 (mux_in_sel[0], opcode[0], opcode[1], opcode[3]);
  and and_17 (and_17_out, ~opcode[0], ~opcode[1], ~opcode[2], ~opcode[3], func[0]);  // AND_Gate
  and and_18 (and_18_out, ~opcode[0], opcode[1]);  // AND_Gate
  or or_5 (ALU_op[0], and_17_out, and_18_out, and_19_out);
  and and_19 (and_19_out, opcode[0], ~opcode[1], opcode[2]);  // AND_Gate
  and and_20 (and_20_out, ~opcode[0], ~opcode[1], ~opcode[2], ~opcode[3], or_1_out);  // AND_Gate
  and and_21 (and_21_out, opcode[1], ~opcode[2], opcode[3]);  // AND_Gate
  and and_22 (and_22_out, opcode[0], opcode[3]);
  and and_23 (and_23_out, opcode[0], ~opcode[1], opcode[2]);  // AND_Gate
  and and_24 (and_24_out, ~opcode[0], opcode[1]);  // AND_Gate
  or or_6 (ALU_src, and_24_out, and_25_out, and_26_out);
  and and_25 (and_25_out, opcode[0], ~opcode[1], ~opcode[2]);  // AND_Gate
  and and_26 (and_26_out, opcode[0], opcode[1], opcode[2], opcode[3]);
  and and_27 (and_27_out, ~opcode[0], ~opcode[1], ~opcode[2], ~opcode[3], func[0], func[1], func[2]);  // AND_Gate
  and and_28 (Eq, and_5_out, not_1_out);
  and and_29 (nEq, and_5_out, opcode[3]);
  or or_7 (reg_WR, nor_1_out, and_6_out, and_7_out, and_8_out, and_9_out);
  or or_8 (ALU_op[2], and_20_out, and_21_out, and_22_out, and_23_out);
  or or_9 (PC_mux[1], and_27_out, and_3_out);
  or or_10 (PC_mux[0], and_27_out, and_4_out);

  assign ALU_op[1] = func[1];
endmodule
