// Logisim project datapath.circ as structural Verilog: 11 circuits, main circuit Datapath
module Datapath (
);

  wire adder_1_cout, alu_1_carry_out, alu_1_zero_flag, and_2_out, and_3_out, and_4_out, and_5_out, and_6_out,
       clock_1_out, comparator_1_eq, Forwarding_forward_rs, Forwarding_forward_rs_exec,
       Forwarding_forward_rt, Forwarding_forward_rt_exec, Hazard_Detection_control_hazard,
       Hazard_Detection_hazard, Hazard_Detection_mem_hazard, IE_MEM_buff_carry_out,
       instruction_decoder_1_p12, instruction_decoder_1_p13, MEM_WB_buff_out_6, nand_1_out, not_1_out,
       or_1_out, subtractor_1_bout;
  wire [0:0] ID_IE_buff_alu_stuff;
  wire [1:0] and_1_out, instruction_decoder_1_p14;
  wire [1:1] instruction_decoder_1_p7;
  wire [2:0] ID_IE_buff_alu_stuff_2, ID_IE_buff_dst_2, ID_IE_buff_rd_wr_controls_2, ID_IE_buff_reg_mux_sel_2,
       IE_MEM_buff_dst_2, IE_MEM_buff_rd_wr_controls_2, IE_MEM_buff_reg_mux_sel_2, instruction_decoder_1_p2,
       instruction_decoder_1_p5, instruction_decoder_1_p6, instruction_decoder_1_p8,
       instruction_decoder_1_p9, instruction_decoder_1_p10, MEM_WB_buff_dst_out, multiplexer_5_out;
  wire [15:0] adder_1_out, alu_1_output, bit_extender_1_out, branch_target_1_bta, Data_Memory_p7,
       Forwarding_forwarded_rs, Forwarding_forwarded_rt, ID_IE_buff_imm_2, ID_IE_buff_pc_1_out,
       ID_IE_buff_rs, ID_IE_buff_rt, IE_MEM_buff_alu_out_2, IE_MEM_buff_imm_out, IE_MEM_buff_pc_1_out,
       IE_MEM_buff_rt_out, IF_ID_buff_ir_out, IF_ID_buff_pc_1_out, instruction_decoder_1_p11,
       MEM_WB_buff_reg_out, multiplexer_1_out, multiplexer_2_out, multiplexer_3_out, multiplexer_4_out,
       multiplexer_6_out, multiplexer_7_out, PC_q, Program_Memory_p8, Register_File_out1, Register_File_out2,
       subtractor_1_out;

  Subtractor #(.width(16)) subtractor_1 (
    .a(multiplexer_2_out), .b(16'h1), .out(subtractor_1_out), .bin(1'b0), .bout(subtractor_1_bout));
  Multiplexer #(.width(16)) multiplexer_1 (
    .in0(multiplexer_2_out), .in1(subtractor_1_out), .out(multiplexer_1_out), .sel(and_5_out), .en(1'b1));
  Register #(.width(16)) PC (.D(multiplexer_1_out), .en(1'b1), .Q(PC_q), .clk(clock_1_out), .clr(1'b0));
  Clock clock_1 (.out(clock_1_out));
  Adder #(.width(16)) adder_1 (.a(PC_q), .b(16'h1), .out(adder_1_out), .cin(1'b0), .cout(adder_1_cout));
  not not_1 (not_1_out, and_6_out);
  Multiplexer #(.select(2), .width(16)) multiplexer_2 (
    .in0(IF_ID_buff_pc_1_out), .in1(instruction_decoder_1_p11), .in2(branch_target_1_bta),
    .in3(multiplexer_3_out), .out(multiplexer_2_out), .sel(and_1_out), .en(1'b1));
  Ftch_Dec_buff IF_ID_buff (
    .PC_1_in(adder_1_out), .PC_1_out(IF_ID_buff_pc_1_out), .IR_in(Program_Memory_p8),
    .IR_out(IF_ID_buff_ir_out), .CLK(clock_1_out), .CLR(and_4_out), .EN(not_1_out));
  // Memory Program_Memory: pin names not known; wires that end beside it: subtractor_1_bout, adder_1_cout, PC_q, 1'b1, 1'b0, clock_1_out, 1'b0, Program_Memory_p8
  // Instruction_Decoder instruction_decoder_1: pin names not known; wires that end beside it: IF_ID_buff_ir_out, instruction_decoder_1_p2[0], instruction_decoder_1_p2[1], instruction_decoder_1_p2[2], instruction_decoder_1_p5, instruction_decoder_1_p6, {instruction_decoder_1_p7[1], and_1_out[0]}, instruction_decoder_1_p8, instruction_decoder_1_p9, instruction_decoder_1_p10, instruction_decoder_1_p11, instruction_decoder_1_p12, instruction_decoder_1_p13, instruction_decoder_1_p14[0], instruction_decoder_1_p14[1]
  and and_1 (and_1_out[1], or_1_out, instruction_decoder_1_p7[1]);
  or or_1 (or_1_out, and_2_out, and_3_out, and_3_out);
  and and_2 (and_2_out, instruction_decoder_1_p7[1], and_1_out[0]);
  and and_3 (and_3_out, instruction_decoder_1_p14[1], ~comparator_1_eq);  // AND_Gate
  and and_4 (and_4_out, nand_1_out, Hazard_Detection_control_hazard);
  and and_5 (and_5_out, nand_1_out, Hazard_Detection_hazard);
  and and_6 (and_6_out, nand_1_out, Hazard_Detection_mem_hazard);
  and and_7 (and_3_out, instruction_decoder_1_p14[0], comparator_1_eq);
  Branch_Target branch_target_1 (
    .PC_1(IF_ID_buff_pc_1_out), .Immediate(instruction_decoder_1_p11), .BTA(branch_target_1_bta));
  nand nand_1 (nand_1_out, ~IF_ID_buff_pc_1_out[0], ~IF_ID_buff_pc_1_out[1], ~IF_ID_buff_pc_1_out[2], ~IF_ID_buff_pc_1_out[3], ~IF_ID_buff_pc_1_out[4], ~IF_ID_buff_pc_1_out[5], ~IF_ID_buff_pc_1_out[6], ~IF_ID_buff_pc_1_out[7], ~IF_ID_buff_pc_1_out[9], ~IF_ID_buff_pc_1_out[10], ~IF_ID_buff_pc_1_out[11], ~IF_ID_buff_pc_1_out[12], ~IF_ID_buff_pc_1_out[13], ~IF_ID_buff_pc_1_out[14], ~IF_ID_buff_pc_1_out[15], ~IF_ID_buff_pc_1_out[8]);  // NAND_Gate
  Hazard Hazard_Detection (
    .beq(and_3_out), .bneq(and_3_out), .forward_Rs_EXEC(Forwarding_forward_rs_exec),
    .forward_Rt_EXEC(Forwarding_forward_rt_exec), .Control_Hazard(Hazard_Detection_control_hazard),
    .Hazard(Hazard_Detection_hazard), .Mem_hazard(Hazard_Detection_mem_hazard),
    .Load(ID_IE_buff_rd_wr_controls_2[2]));
  Multiplexer #(.width(16)) multiplexer_3 (
    .in0(Register_File_out1), .in1(Forwarding_forwarded_rs), .out(multiplexer_3_out),
    .sel(Forwarding_forward_rs), .en(1'b1));
  Register_File Register_File (
    .WR_en(MEM_WB_buff_out_6), .IN_sel(MEM_WB_buff_dst_out), .Data_IN(MEM_WB_buff_reg_out),
    .OUT1_sel(instruction_decoder_1_p8), .OUT2_sel(instruction_decoder_1_p9), .CLK(clock_1_out),
    .OUT1(Register_File_out1), .OUT2(Register_File_out2));
  Comparator #(.width(16)) comparator_1 (
    .a(multiplexer_3_out), .b(multiplexer_4_out), .eq(comparator_1_eq));  // open: gt, lt
  Multiplexer #(.width(16)) multiplexer_4 (
    .in0(Register_File_out2), .in1(Forwarding_forwarded_rt), .out(multiplexer_4_out),
    .sel(Forwarding_forward_rt), .en(1'b1));
  Multiplexer #(.width(3)) multiplexer_5 (
    .in0(instruction_decoder_1_p10), .in1(instruction_decoder_1_p9), .out(multiplexer_5_out),
    .sel(instruction_decoder_1_p13), .en(1'b1));
  Dec_Exec_buff ID_IE_buff (
    .RD_WR_controls(instruction_decoder_1_p2), .reg_mux_sel(instruction_decoder_1_p5),
    .ALU_src(instruction_decoder_1_p12), .ALU_op(instruction_decoder_1_p6), .ALU_src1(multiplexer_3_out),
    .ALU_src2(multiplexer_4_out), .IMM(instruction_decoder_1_p11), .CLK(clock_1_out),
    .CLR(Hazard_Detection_mem_hazard), .RD_WR_controls_2(ID_IE_buff_rd_wr_controls_2),
    .reg_mux_sel_2(ID_IE_buff_reg_mux_sel_2),
    .ALU_stuff({ID_IE_buff_alu_stuff_2[0], ID_IE_buff_alu_stuff_2[1], ID_IE_buff_alu_stuff_2[2], ID_IE_buff_alu_stuff[0]}),
    .Rs(ID_IE_buff_rs), .Rt(ID_IE_buff_rt), .IMM_2(ID_IE_buff_imm_2), .DST(multiplexer_5_out),
    .DST_2(ID_IE_buff_dst_2), .PC_1_in(IF_ID_buff_pc_1_out), .PC_1_out(ID_IE_buff_pc_1_out));
  Forwarding Forwarding (
    .Rs(instruction_decoder_1_p8), .Rt(instruction_decoder_1_p9), .forwarded_rs(Forwarding_forwarded_rs),
    .forward_rs(Forwarding_forward_rs), .forwarded_rt(Forwarding_forwarded_rt),
    .forward_rt(Forwarding_forward_rt), .ALU_forward(alu_1_output), .MEM_forward(Data_Memory_p7),
    .ALU_dst(ID_IE_buff_dst_2), .MEM_dst(IE_MEM_buff_dst_2), .forward_rs_EXEC(Forwarding_forward_rs_exec),
    .forward_rt_EXEC(Forwarding_forward_rt_exec));
  Multiplexer #(.width(16)) multiplexer_6 (
    .in0(ID_IE_buff_rt), .in1(ID_IE_buff_imm_2), .out(multiplexer_6_out), .sel(ID_IE_buff_alu_stuff[0]),
    .en(1'b1));
  ALU alu_1 (
    .source_1(ID_IE_buff_rs), .source_2(multiplexer_6_out), .alu_op(ID_IE_buff_alu_stuff_2),
    .\output (alu_1_output), .alu_en(1'b1), .carry_out(alu_1_carry_out), .Zero_flag(alu_1_zero_flag));
  Exec_Mem_buff IE_MEM_buff (
    .PC_1_in(ID_IE_buff_pc_1_out), .RD_WR_controls(ID_IE_buff_rd_wr_controls_2),
    .reg_mux_sel(ID_IE_buff_reg_mux_sel_2), .ALU_out(alu_1_output), .DST(ID_IE_buff_dst_2),
    .Zero(alu_1_zero_flag), .Carry_Sign(alu_1_carry_out), .CLK(clock_1_out), .CLR(1'b0),
    .PC_1_out(IE_MEM_buff_pc_1_out), .RD_WR_controls_2(IE_MEM_buff_rd_wr_controls_2),
    .reg_mux_sel_2(IE_MEM_buff_reg_mux_sel_2), .ALU_out_2(IE_MEM_buff_alu_out_2), .DST_2(IE_MEM_buff_dst_2),
    .Carry_out(IE_MEM_buff_carry_out), .Rt_in(ID_IE_buff_rt), .Rt_out(IE_MEM_buff_rt_out),
    .IMM_in(ID_IE_buff_imm_2), .IMM_out(IE_MEM_buff_imm_out));  // open: Zero_out
  // Memory Data_Memory: pin names not known; wires that end beside it: IE_MEM_buff_alu_out_2, IE_MEM_buff_rt_out, IE_MEM_buff_rd_wr_controls_2[2], IE_MEM_buff_rd_wr_controls_2[1], clock_1_out, 1'b0, Data_Memory_p7
  assign bit_extender_1_out = {{15{1'b0}}, IE_MEM_buff_carry_out};  // Bit_Extender bit_extender_1
  Mem_WB_buff MEM_WB_buff (
    .reg_WR(IE_MEM_buff_rd_wr_controls_2[0]), .DST_in(IE_MEM_buff_dst_2), .REG_in(multiplexer_7_out),
    .CLK(clock_1_out), .CLR(1'b0), .out_6(MEM_WB_buff_out_6), .DST_out(MEM_WB_buff_dst_out),
    .REG_out(MEM_WB_buff_reg_out));
  Multiplexer #(.select(3), .width(16)) multiplexer_7 (
    .in0(IE_MEM_buff_alu_out_2), .in1(bit_extender_1_out), .in3(Data_Memory_p7), .in4(IE_MEM_buff_pc_1_out),
    .in5(IE_MEM_buff_pc_1_out), .in6(IE_MEM_buff_imm_out), .in7(IE_MEM_buff_imm_out),
    .out(multiplexer_7_out), .sel(IE_MEM_buff_reg_mux_sel_2), .en(1'b1));  // open: in2

  // Notes on the sheet:
  //   MEM forward bus
endmodule

module Ftch_Dec_buff (
  input  [15:0] PC_1_in,
  input  [15:0] IR_in,
  input  CLK,
  input  CLR,
  input  EN,
  output [15:0] PC_1_out,
  output [15:0] IR_out
);

  Register #(.width(16), .trigger("falling")) register_1 (.D(PC_1_in), .en(EN), .Q(PC_1_out), .clk(CLK), .clr(CLR));
  Register #(.width(16), .trigger("falling")) Instruction_Register (
    .D(IR_in), .en(EN), .Q(IR_out), .clk(CLK), .clr(CLR));
endmodule

module Fetch2_0 (
  input  [15:0] PC_1_in,
  input  [15:0] IR_in,
  input  CLK,
  input  CLR,
  input  EN,
  output [15:0] PC_1_out,
  output [15:0] IR_out
);

  My_Reg my_reg_1 (.Data_in(PC_1_in), .CLK(CLK), .EN(EN), .CLR(CLR), .out_5(PC_1_out));
  My_Reg my_reg_2 (.Data_in(IR_in), .CLK(CLK), .EN(EN), .CLR(CLR), .out_5(IR_out));
endmodule

module Dec_Exec_buff (
  input  [15:0] PC_1_in,
  input  [2:0] RD_WR_controls,
  input  [2:0] reg_mux_sel,
  input  ALU_src,
  input  [2:0] ALU_op,
  input  [15:0] ALU_src1,
  input  [15:0] ALU_src2,
  input  [15:0] IMM,
  input  [2:0] DST,
  input  CLK,
  input  CLR,
  output [15:0] PC_1_out,
  output [2:0] RD_WR_controls_2,
  output [2:0] reg_mux_sel_2,
  output [3:0] ALU_stuff,
  output [15:0] Rs,
  output [15:0] Rt,
  output [15:0] IMM_2,
  output [2:0] DST_2
);

  Register #(.width(16), .trigger("falling")) register_1 (.D(PC_1_in), .en(1'b1), .Q(PC_1_out), .clk(CLK), .clr(CLR));
  Register #(.width(3), .trigger("falling")) register_2 (
    .D(RD_WR_controls), .en(1'b1), .Q(RD_WR_controls_2), .clk(CLK), .clr(CLR));
  Register #(.width(3), .trigger("falling")) register_3 (
    .D(reg_mux_sel), .en(1'b1), .Q(reg_mux_sel_2), .clk(CLK), .clr(CLR));
  Register #(.width(4), .trigger("falling")) register_4 (
    .D({ALU_op, ALU_src}), .en(1'b1), .Q(ALU_stuff), .clk(CLK), .clr(CLR));
  Register #(.width(16), .trigger("falling")) register_5 (.D(ALU_src1), .en(1'b1), .Q(Rs), .clk(CLK), .clr(CLR));
  Register #(.width(16), .trigger("falling")) register_6 (.D(ALU_src2), .en(1'b1), .Q(Rt), .clk(CLK), .clr(CLR));
  Register #(.width(16), .trigger("falling")) register_7 (.D(IMM), .en(1'b1), .Q(IMM_2), .clk(CLK), .clr(CLR));
  Register #(.width(3), .trigger("falling")) register_8 (.D(DST), .en(1'b1), .Q(DST_2), .clk(CLK), .clr(CLR));

  // Notes on the sheet:
  //   Modify clear for stalls
  //   Registers are falling edge here .... Read is achieved on rising edge the second half of the signal
endmodule

module Exec_Mem_buff (
  input  [15:0] IMM_in,
  input  [15:0] Rt_in,
  input  [15:0] PC_1_in,
  input  [2:0] RD_WR_controls,
  input  [2:0] reg_mux_sel,
  input  [15:0] ALU_out,
  input  [2:0] DST,
  input  Zero,
  input  Carry_Sign,
  input  CLK,
  input  CLR,
  output [15:0] IMM_out,
  output [15:0] Rt_out,
  output [15:0] PC_1_out,
  output [2:0] RD_WR_controls_2,
  output [2:0] reg_mux_sel_2,
  output [15:0] ALU_out_2,
  output [2:0] DST_2,
  output Zero_out,
  output Carry_out
);

  Register #(.width(16), .trigger("falling")) register_1 (.D(IMM_in), .en(1'b1), .Q(IMM_out), .clk(CLK), .clr(CLR));
  Register #(.width(16), .trigger("falling")) register_2 (.D(Rt_in), .en(1'b1), .Q(Rt_out), .clk(CLK), .clr(CLR));
  Register #(.width(16), .trigger("falling")) register_3 (.D(PC_1_in), .en(1'b1), .Q(PC_1_out), .clk(CLK), .clr(CLR));
  Register #(.width(3), .trigger("falling")) register_4 (
    .D(RD_WR_controls), .en(1'b1), .Q(RD_WR_controls_2), .clk(CLK), .clr(CLR));
  Register #(.width(3), .trigger("falling")) register_5 (
    .D(reg_mux_sel), .en(1'b1), .Q(reg_mux_sel_2), .clk(CLK), .clr(CLR));
  Register #(.width(16), .trigger("falling")) register_6 (.D(ALU_out), .en(1'b1), .Q(ALU_out_2), .clk(CLK), .clr(CLR));
  Register #(.width(3), .trigger("falling")) register_7 (.D(DST), .en(1'b1), .Q(DST_2), .clk(CLK), .clr(CLR));
  Register #(.width(1), .trigger("falling")) register_8 (.D(Zero), .en(1'b1), .Q(Zero_out), .clk(CLK), .clr(CLR));
  Register #(.width(1), .trigger("falling")) register_9 (
    .D(Carry_Sign), .en(1'b1), .Q(Carry_out), .clk(CLK), .clr(CLR));

  // Notes on the sheet:
  //   Registers are falling edge here .... Read is achieved on rising edge the second half of the signal
endmodule

module Mem_WB_buff (
  input  reg_WR,
  input  [2:0] DST_in,
  input  [15:0] REG_in,
  input  CLK,
  input  CLR,
  output out_6,
  output [2:0] DST_out,
  output [15:0] REG_out
);

  Register #(.width(1), .trigger("falling")) register_1 (.D(reg_WR), .en(1'b1), .Q(out_6), .clk(CLK), .clr(CLR));
  Register #(.width(3), .trigger("falling")) register_2 (.D(DST_in), .en(1'b1), .Q(DST_out), .clk(CLK), .clr(CLR));
  Register #(.width(16), .trigger("falling")) register_3 (.D(REG_in), .en(1'b1), .Q(REG_out), .clk(CLK), .clr(CLR));

  // Notes on the sheet:
  //   Registers are falling edge here .... Read is achieved on rising edge the second half of the signal
endmodule

module Forwarding (
  input  [15:0] ALU_forward,
  input  [2:0] Rs,
  input  [2:0] Rt,
  input  [15:0] MEM_forward,
  input  [2:0] ALU_dst,
  input  [2:0] MEM_dst,
  output forward_rt_EXEC,
  output forward_rs_EXEC,
  output [15:0] forwarded_rs,
  output forward_rs,
  output [15:0] forwarded_rt,
  output forward_rt
);

  wire comparator_2_eq, comparator_4_eq, not_1_out, not_2_out;

  Multiplexer #(.width(16)) multiplexer_1 (
    .in0(ALU_forward), .in1(MEM_forward), .out(forwarded_rs), .sel(not_1_out), .en(forward_rs));
  Multiplexer #(.width(16)) multiplexer_2 (
    .in0(ALU_forward), .in1(MEM_forward), .out(forwarded_rt), .sel(not_2_out), .en(forward_rt));
  not not_1 (not_1_out, forward_rs_EXEC);
  or or_1 (forward_rs, forward_rs_EXEC, comparator_2_eq);
  not not_2 (not_2_out, forward_rt_EXEC);
  or or_2 (forward_rt, forward_rt_EXEC, comparator_4_eq);
  Comparator #(.width(3)) comparator_1 (.a(Rs), .b(ALU_dst), .eq(forward_rs_EXEC));  // open: gt, lt
  Comparator #(.width(3)) comparator_2 (.a(Rs), .b(MEM_dst), .eq(comparator_2_eq));  // open: gt, lt
  Comparator #(.width(3)) comparator_3 (.a(Rt), .b(ALU_dst), .eq(forward_rt_EXEC));  // open: gt, lt
  Comparator #(.width(3)) comparator_4 (.a(Rt), .b(MEM_dst), .eq(comparator_4_eq));  // open: gt, lt
endmodule

module Hazard (
  input  beq,
  input  bneq,
  input  Load,
  input  forward_Rs_EXEC,
  input  forward_Rt_EXEC,
  output Control_Hazard,
  output Hazard,
  output Mem_hazard
);

  wire or_1_out;

  or or_1 (or_1_out, forward_Rs_EXEC, forward_Rt_EXEC);
  xor xor_1 (Control_Hazard, beq, bneq);
  and and_1 (Mem_hazard, Load, or_1_out);
  or or_2 (Hazard, Control_Hazard, Mem_hazard);

  // Notes on the sheet:
  //   Control Hazard
endmodule

// BTA
module Branch_Target (
  input  [15:0] PC_1,
  input  [15:0] Immediate,
  output [15:0] BTA
);

  wire [15:0] subtractor_1_out;

  Subtractor #(.width(16)) subtractor_1 (.a(PC_1), .b(16'h1), .out(subtractor_1_out));  // open: bin, bout
  Adder #(.width(16)) adder_1 (.a(subtractor_1_out), .b(Immediate), .out(BTA));  // open: cin, cout
endmodule

module Tmp (
  input  [15:0] in_1,
  input  [15:0] in_2,
  output [15:0] out_3,
  output [15:0] out_4
);

  wire clock_1_out;
  wire [15:0] undriven;

  Clock clock_1 (.out(clock_1_out));
  Ftch_Dec_buff ftch_dec_buff_1 (
    .PC_1_in(in_1), .PC_1_out(out_3), .IR_in(in_2), .IR_out(out_4), .CLK(clock_1_out), .CLR(1'b0), .EN(1'b1));
  // NAND_Gate nand_1 has open pins: in0=undriven[0], in1=undriven[1], in2=undriven[2], in3=undriven[3], in4=undriven[4], in5=undriven[5], in6=undriven[6], in7=undriven[7], in8=undriven[9], in9=undriven[10], in10=undriven[11], in11=undriven[12], in12=undriven[13], in13=undriven[14], in14=undriven[15], in15=undriven[8], out=open
endmodule

module My_Reg (
  input  [15:0] Data_in,
  input  CLK,
  input  EN,
  input  CLR,
  output [15:0] out_5
);

  D_Flip_Flop #(.trigger("falling")) d_ff_1 (
    .clk(CLK), .D(Data_in[0]), .Q(out_5[0]), .preset(1'b0), .en(EN), .reset(CLR));  // open: Qn
  D_Flip_Flop #(.trigger("falling")) d_ff_2 (
    .clk(CLK), .D(Data_in[1]), .Q(out_5[1]), .preset(1'b0), .en(EN), .reset(CLR));  // open: Qn
  D_Flip_Flop #(.trigger("falling")) d_ff_3 (
    .clk(CLK), .D(Data_in[2]), .Q(out_5[2]), .preset(1'b0), .en(EN), .reset(CLR));  // open: Qn
  D_Flip_Flop #(.trigger("falling")) d_ff_4 (
    .clk(CLK), .D(Data_in[3]), .Q(out_5[3]), .preset(1'b0), .en(EN), .reset(CLR));  // open: Qn
  D_Flip_Flop #(.trigger("falling")) d_ff_5 (
    .clk(CLK), .D(Data_in[4]), .Q(out_5[4]), .preset(1'b0), .en(EN), .reset(CLR));  // open: Qn
  D_Flip_Flop #(.trigger("falling")) d_ff_6 (
    .clk(CLK), .D(Data_in[5]), .Q(out_5[5]), .preset(1'b0), .en(EN), .reset(CLR));  // open: Qn
  D_Flip_Flop #(.trigger("falling")) d_ff_7 (
    .clk(CLK), .D(Data_in[6]), .Q(out_5[6]), .preset(1'b0), .en(EN), .reset(CLR));  // open: Qn
  D_Flip_Flop #(.trigger("falling")) d_ff_8 (
    .clk(CLK), .D(Data_in[7]), .Q(out_5[7]), .preset(1'b0), .en(EN), .reset(CLR));  // open: Qn
  D_Flip_Flop #(.trigger("falling")) d_ff_9 (
    .clk(CLK), .D(Data_in[8]), .Q(out_5[8]), .preset(1'b0), .en(EN), .reset(CLR));  // open: Qn
  D_Flip_Flop #(.trigger("falling")) d_ff_10 (
    .clk(CLK), .D(Data_in[9]), .Q(out_5[9]), .preset(1'b0), .en(EN), .reset(CLR));  // open: Qn
  D_Flip_Flop #(.trigger("falling")) d_ff_11 (
    .clk(CLK), .D(Data_in[10]), .Q(out_5[10]), .preset(1'b0), .en(EN), .reset(CLR));  // open: Qn
  D_Flip_Flop #(.trigger("falling")) d_ff_12 (
    .clk(CLK), .D(Data_in[11]), .Q(out_5[11]), .preset(1'b0), .en(EN), .reset(CLR));  // open: Qn
  D_Flip_Flop #(.trigger("falling")) d_ff_13 (
    .clk(CLK), .D(Data_in[12]), .Q(out_5[12]), .preset(1'b0), .en(EN), .reset(CLR));  // open: Qn
  D_Flip_Flop #(.trigger("falling")) d_ff_14 (
    .clk(CLK), .D(Data_in[13]), .Q(out_5[13]), .preset(1'b0), .en(EN), .reset(CLR));  // open: Qn
  D_Flip_Flop #(.trigger("falling")) d_ff_15 (
    .clk(CLK), .D(Data_in[14]), .Q(out_5[14]), .preset(1'b0), .en(EN), .reset(CLR));  // open: Qn
  D_Flip_Flop #(.trigger("falling")) d_ff_16 (
    .clk(CLK), .D(Data_in[15]), .Q(out_5[15]), .preset(1'b0), .en(EN), .reset(CLR));  // open: Qn
endmodule
