// Logisim project decoding_stage(1).circ as structural Verilog: 1 circuit, main circuit Instruction Decoder
module Instruction_Decoder (
  input  [15:0] Instruction,
  output reg_WR,
  output mem_WR,
  output mem_RD,
  output [2:0] RegWriteMux,
  output [2:0] ALU_op,
  output ALU_src,
  output [1:0] PCMUX_sel,
  output DST_sel,
  output Eq,
  output nEq,
  output [2:0] Rs,
  output [2:0] Rd,
  output [2:0] Rt,
  output [15:0] Sign_Extended_Immediate
);

  wire or_1_out;
  wire [1:0] and_1_out;
  wire [15:0] bit_extender_1_out, Extender_out, shifter_by4_1_out;

  and and_1 (and_1_out[0], Instruction[12], ~Instruction[13], Instruction[14], Instruction[15]);  // AND_Gate
  and and_2 (and_1_out[1], Instruction[12], Instruction[13], Instruction[14], Instruction[15]);
  or or_1 (or_1_out, and_1_out[1], and_1_out[0]);
  Sign_Extender Extender (.In(Instruction[5:0]), .Out(Extender_out));
  assign bit_extender_1_out = {{4{Instruction[11]}}, Instruction[11:0]};  // Bit_Extender bit_extender_1
  // Control_Unit Control: pin names not known; wires that end beside it: {Instruction[12], Instruction[13], Instruction[14], Instruction[15]}, {Instruction[0], Instruction[1], Instruction[2]}, reg_WR, mem_WR, mem_RD, RegWriteMux, ALU_op, ALU_src, PCMUX_sel, DST_sel, Eq, nEq
  Shifter_by4 shifter_by4_1 (.In(bit_extender_1_out), .Out(shifter_by4_1_out));
  Multiplexer #(.width(3)) multiplexer_1 (.in0(Instruction[11:9]), .in1(3'b000), .out(Rs), .sel(or_1_out), .en(1'b1));
  Multiplexer #(.select(2), .width(3)) multiplexer_2 (
    .in0(Instruction[8:6]), .in1(3'b111), .in2(3'b001), .out(Rt), .sel(and_1_out), .en(1'b1));  // open: in3
  Multiplexer #(.select(2), .width(16)) multiplexer_3 (
    .in0(Extender_out), .in1(bit_extender_1_out), .in2(shifter_by4_1_out), .out(Sign_Extended_Immediate),
    .sel(and_1_out), .en(1'b1));  // open: in3

  assign Rd = Instruction[5:3];
endmodule
