// Logisim project extender.circ as structural Verilog: 1 circuit, main circuit main
module main (
  input  [9:0] in_1,
  output [23:0] out_2
);


  assign out_2 = {{15{in_1[9]}}, in_1[8:0]};
endmodule
