// Logisim project in.circ as structural Verilog: 1 circuit, main circuit main
module main (
  output out_1,
  output [7:0] out_2
);

  wire button_1_out, clock_1_out, comparator_1_eq;
  wire [6:0] keyboard_1_data;
  wire [15:0] counter_1_q;

  Comparator comparator_1 (.a(out_2), .b(8'ha), .eq(comparator_1_eq));  // open: gt, lt
  Clock clock_1 (.out(clock_1_out));
  Counter #(.width(16), .max('hffff)) counter_1 (
    .count(comparator_1_eq), .Q(counter_1_q), .clk(clock_1_out));  // open: load, D, carry, clr
  TTY tty_1 (.data(keyboard_1_data), .clk(clock_1_out), .we(1'b1), .clr(button_1_out));
  Keyboard keyboard_1 (.clk(clock_1_out), .re(1'b1), .clr(button_1_out), .avail(out_1), .data(keyboard_1_data));
  Button button_1 (.out(button_1_out));
  RAM #(.addrWidth(16)) ram_1 (.addr(counter_1_q), .data(out_2), .clk(clock_1_out), .ld(1'b0));  // open: sel, clr
  assign out_2 = {{1{1'b0}}, keyboard_1_data};  // Bit_Extender bit_extender_1
endmodule
