// Logisim project mainControl.circ as structural Verilog: 1 circuit, main circuit main
module main (
  input  [4:0] opcode,
  input  SF_BIT,
  output [1:0] Alu_Op,
  output j,
  output memRd,
  output jr,
  output memWr,
  output jal,
  output AluSrc,
  output BEQ,
  output regWr,
  output regDst,
  output sf_flag,
  output EXTop,
  output wb
);

  wire and_6_out, and_7_out, and_8_out, and_9_out, and_10_out, and_11_out, and_12_out, and_13_out,
       and_15_out, and_16_out, and_17_out, and_18_out, and_19_out, and_20_out, and_21_out, and_22_out,
       and_23_out, and_24_out, or_1_out, or_2_out, or_3_out, or_4_out;

  and and_1 (j, ~opcode[0], ~opcode[1], opcode[2], opcode[3], ~opcode[4]);  // AND_Gate
  and and_2 (jr, ~opcode[0], opcode[1], opcode[2], ~opcode[3], ~opcode[4]);  // AND_Gate
  and and_3 (jal, opcode[0], ~opcode[1], opcode[2], opcode[3], ~opcode[4]);  // AND_Gate
  and and_4 (BEQ, ~opcode[0], opcode[1], opcode[2], opcode[3], ~opcode[4]);  // AND_Gate
  and and_5 (sf_flag, BEQ, SF_BIT);
  and and_6 (and_6_out, ~opcode[0], opcode[1]);  // AND_Gate
  and and_7 (and_7_out, ~opcode[1], opcode[3]);  // AND_Gate
  and and_8 (and_8_out, opcode[1], ~opcode[2], ~opcode[4]);  // AND_Gate
  and and_9 (and_9_out, ~opcode[1], opcode[2]);  // AND_Gate
  and and_10 (and_10_out, opcode[0], ~opcode[1], ~opcode[3]);  // AND_Gate
  and and_11 (and_11_out, opcode[1], opcode[3]);
  and and_12 (and_12_out, opcode[0], ~opcode[1], ~opcode[2], opcode[3], ~opcode[4]);  // AND_Gate
  and and_13 (and_13_out, ~opcode[0], opcode[1], ~opcode[2], ~opcode[3], ~opcode[4]);  // AND_Gate
  and and_14 (memWr, ~opcode[0], opcode[1], ~opcode[2], opcode[3], ~opcode[4]);  // AND_Gate
  and and_15 (and_15_out, ~opcode[0], opcode[3]);  // AND_Gate
  and and_16 (and_16_out, ~opcode[1], opcode[3]);  // AND_Gate
  and and_17 (and_17_out, opcode[1], opcode[2]);
  or or_1 (or_1_out, ~opcode[1], opcode[2], ~opcode[3]);  // OR_Gate
  or or_2 (or_2_out, ~opcode[0], opcode[1], ~opcode[2], opcode[3]);  // OR_Gate
  or or_3 (or_3_out, opcode[0], ~opcode[1], ~opcode[2], opcode[3]);  // OR_Gate
  or or_4 (or_4_out, opcode[0], opcode[1], ~opcode[2], ~opcode[3]);  // OR_Gate
  and and_18 (and_18_out, ~opcode[1], ~opcode[3]);  // AND_Gate
  and and_19 (and_19_out, ~opcode[2], ~opcode[3]);  // AND_Gate
  and and_20 (and_20_out, opcode[0], opcode[1], opcode[2], ~opcode[3], ~opcode[4]);  // AND_Gate
  and and_21 (and_21_out, ~opcode[0], opcode[3], ~opcode[4]);  // AND_Gate
  and and_22 (and_22_out, ~opcode[1], opcode[3], ~opcode[4]);  // AND_Gate
  and and_23 (and_23_out, opcode[0], opcode[3]);
  and and_24 (and_24_out, ~opcode[0], opcode[1], ~opcode[2]);  // AND_Gate
  or or_5 (Alu_Op[0], and_6_out, and_7_out, and_8_out);
  or or_6 (Alu_Op[1], and_9_out, and_10_out, and_11_out);
  or or_7 (memRd, and_12_out, and_13_out);
  or or_8 (AluSrc, and_15_out, and_16_out, and_17_out);
  or or_9 (regDst, and_18_out, and_19_out);
  or or_10 (EXTop, and_20_out, and_21_out, and_22_out);
  or or_11 (wb, and_23_out, and_24_out);
  and and_25 (regWr, or_1_out, or_2_out, or_3_out, or_4_out);
endmodule
