// Logisim project mem_block(1).circ as structural Verilog: 1 circuit, main circuit Memory
module Memory (
  input  [15:0] Address,
  input  [15:0] Data_IN,
  input  RD,
  input  WR,
  input  CLK,
  input  CLR,
  output [15:0] Data_OUT
);

  wire not_1_out, not_2_out, or_1_out;
  wire [15:0] ram_1_data;

  or or_1 (or_1_out, RD, WR);
  not not_1 (not_1_out, WR);
  assign Data_OUT = not_2_out ? ram_1_data : 16'bz;  // Controlled_Buffer controlled_buffer_1
  RAM #(.addrWidth(16), .dataWidth(16)) ram_1 (
    .addr(Address), .data(ram_1_data), .sel(or_1_out), .clk(CLK), .ld(not_1_out), .clr(CLR));
  assign ram_1_data = WR ? Data_IN : 16'bz;  // Controlled_Buffer controlled_buffer_2
  not not_2 (not_2_out, WR);
endmodule
