// Logisim project regFile_final.circ as structural Verilog: 1 circuit, main circuit main
module main (
  input  Wr_en,
  input  [2:0] RA,
  input  [2:0] RW,
  input  [2:0] RB,
  input  [23:0] Data_in,
  input  Data_in_2,
  output [23:0] BusA,
  output [23:0] BusB
);

  wire and_1_out, and_2_out, and_3_out, and_4_out, and_5_out, and_6_out, and_7_out, decoder_1_out0,
       decoder_1_out1, decoder_1_out2, decoder_1_out3, decoder_1_out4, decoder_1_out5, decoder_1_out6,
       decoder_1_out7;
  wire [23:0] register_1_q, register_2_q, register_3_q, register_4_q, register_5_q, register_6_q,
       register_7_q;

  Decoder #(.select(3)) decoder_1 (
    .out0(decoder_1_out0), .out1(decoder_1_out1), .out2(decoder_1_out2), .out3(decoder_1_out3),
    .out4(decoder_1_out4), .out5(decoder_1_out5), .out6(decoder_1_out6), .out7(decoder_1_out7), .sel(RW));  // open: en
  and and_1 (and_1_out, decoder_1_out1, Wr_en);
  and and_2 (and_2_out, decoder_1_out2, Wr_en);
  and and_3 (and_3_out, decoder_1_out3, Wr_en);
  and and_4 (and_4_out, decoder_1_out4, Wr_en);
  and and_5 (and_5_out, decoder_1_out5, Wr_en);
  and and_6 (and_6_out, decoder_1_out6, Wr_en);
  and and_7 (and_7_out, decoder_1_out7, Wr_en);
  Register #(.width(24)) register_1 (.D(Data_in), .en(and_1_out), .Q(register_1_q), .clk(Data_in_2), .clr(1'b0));
  Register #(.width(24)) register_2 (.D(Data_in), .en(and_2_out), .Q(register_2_q), .clk(Data_in_2), .clr(1'b0));
  Register #(.width(24)) register_3 (.D(Data_in), .en(and_3_out), .Q(register_3_q), .clk(Data_in_2), .clr(1'b0));
  Register #(.width(24)) register_4 (.D(Data_in), .en(and_4_out), .Q(register_4_q), .clk(Data_in_2), .clr(1'b0));
  Register #(.width(24)) register_5 (.D(Data_in), .en(and_5_out), .Q(register_5_q), .clk(Data_in_2), .clr(1'b0));
  Register #(.width(24)) register_6 (.D(Data_in), .en(and_6_out), .Q(register_6_q), .clk(Data_in_2), .clr(1'b0));
  Register #(.width(24)) register_7 (.D(Data_in), .en(and_7_out), .Q(register_7_q), .clk(Data_in_2), .clr(1'b0));
  Multiplexer #(.select(3), .width(24)) multiplexer_1 (
    .in0({24{1'b0}}), .in1(register_1_q), .in2(register_2_q), .in3(register_3_q), .in4(register_4_q),
    .in5(register_5_q), .in6(register_6_q), .in7(register_7_q), .out(BusA), .sel(RA), .en(1'b1));
  Multiplexer #(.select(3), .width(24)) multiplexer_2 (
    .in0({24{1'b0}}), .in1(register_1_q), .in2(register_2_q), .in3(register_3_q), .in4(register_4_q),
    .in5(register_5_q), .in6(register_6_q), .in7(register_7_q), .out(BusB), .sel(RB), .en(1'b1));
endmodule
