// Logisim project regfile.circ as structural Verilog: 1 circuit, main circuit Register File
module Register_File (
  input  WR_en,
  input  [2:0] IN_sel,
  input  [15:0] Data_IN,
  input  [2:0] OUT1_sel,
  input  [2:0] OUT2_sel,
  input  CLK,
  output [15:0] OUT1,
  output [15:0] OUT2
);

  wire decoder_1_out0, decoder_1_out1, decoder_1_out2, decoder_1_out3, decoder_1_out4, decoder_1_out5,
       decoder_1_out6, decoder_1_out7;
  wire [15:0] register_1_q, register_2_q, register_3_q, register_4_q, register_5_q, register_6_q,
       register_7_q;

  Decoder #(.select(3)) decoder_1 (
    .out0(decoder_1_out0), .out1(decoder_1_out1), .out2(decoder_1_out2), .out3(decoder_1_out3),
    .out4(decoder_1_out4), .out5(decoder_1_out5), .out6(decoder_1_out6), .out7(decoder_1_out7), .sel(IN_sel),
    .en(WR_en));
  Register #(.width(16)) register_1 (.D(Data_IN), .en(decoder_1_out1), .Q(register_1_q), .clk(CLK), .clr(1'b0));
  Register #(.width(16)) register_2 (.D(Data_IN), .en(decoder_1_out2), .Q(register_2_q), .clk(CLK), .clr(1'b0));
  Register #(.width(16)) register_3 (.D(Data_IN), .en(decoder_1_out3), .Q(register_3_q), .clk(CLK), .clr(1'b0));
  Register #(.width(16)) register_4 (.D(Data_IN), .en(decoder_1_out4), .Q(register_4_q), .clk(CLK), .clr(1'b0));
  Register #(.width(16)) register_5 (.D(Data_IN), .en(decoder_1_out5), .Q(register_5_q), .clk(CLK), .clr(1'b0));
  Register #(.width(16)) register_6 (.D(Data_IN), .en(decoder_1_out6), .Q(register_6_q), .clk(CLK), .clr(1'b0));
  Register #(.width(16)) register_7 (.D(Data_IN), .en(decoder_1_out7), .Q(register_7_q), .clk(CLK), .clr(1'b0));
  Multiplexer #(.select(3), .width(16)) multiplexer_1 (
    .in0({16{1'b0}}), .in1(register_1_q), .in2(register_2_q), .in3(register_3_q), .in4(register_4_q),
    .in5(register_5_q), .in6(register_6_q), .in7(register_7_q), .out(OUT1), .sel(OUT1_sel), .en(1'b1));
  Multiplexer #(.select(3), .width(16)) multiplexer_2 (
    .in0({16{1'b0}}), .in1(register_1_q), .in2(register_2_q), .in3(register_3_q), .in4(register_4_q),
    .in5(register_5_q), .in6(register_6_q), .in7(register_7_q), .out(OUT2), .sel(OUT2_sel), .en(1'b1));
endmodule
