// Logisim project shifterby4.circ as structural Verilog: 1 circuit, main circuit main
module main (
  input  [23:0] in_1,
  output [23:0] out_2
);


  assign out_2 = {in_1[19:0], 4'b0000};
endmodule
