// Logisim project sign.circ as structural Verilog: 2 circuits, main circuit Sign Extender
module Sign_Extender (
  input  [5:0] In,
  output [15:0] Out
);


  assign Out = {{11{In[5]}}, In[4:0]};
endmodule

module Shifter_by4 (
  input  [15:0] In,
  output [15:0] Out
);


  assign Out = {In[11:0], 4'b0000};
endmodule
